# Fritzing sketch wire (saved by Fritzing 0.9.3b)

parts:
  WeMos_D1_Mini1 = WeMos D1 Mini
  元件1 = Adafruit VL530X Time of Flight Distance Sensor [part_number="first vl53l1x"]
  元件2 = Adafruit VL530X Time of Flight Distance Sensor [part_number="second vl53l1x"]

nets:
  5V: WeMos_D1_Mini1.5V, 元件1.VCC
  N1: WeMos_D1_Mini1.D1, 元件1.SCL, 元件2.SCL
  N2: WeMos_D1_Mini1.D2, 元件1.SDA, 元件2.SDA
  N3: WeMos_D1_Mini1.D3, 元件1.XSHUT
  N4: WeMos_D1_Mini1.D4, 元件2.GPIO, 元件2.XSHUT
  N5: WeMos_D1_Mini1.G, 元件1.GND

custom parts:
  Adafruit VL530X Time of Flight Distance Sensor: The VL53L0X is a Time of Flight distance sensor like no other you've used! The sensor contains a very tiny invisible laser source, and a matching sensor. The VL53L0X can detect the "time of flight", or how long the light has taken to bounce back to the sensor. Since it uses a very narrow light source, it is good for determining distance of only the surface directly in front of it. Unlike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
